// Logisim project hw4.circ as structural Verilog: 6 circuits, main circuit main
module main (
  input  reset
);

  wire alusrc, and_1_out, and_2_out, blt, bne, clk, equal, \input , j, jal, jr, jump, keyboard_1_avail, mem,
       not_1_out, not_2_out, \output , rdst, rwd, rwe, shift, sign;
  wire [2:0] instructiondecoder_1_rd, multiplexer_3_out, rs, rt, shamt, writereg;
  wire [3:0] opcode;
  wire [5:0] imm;
  wire [6:0] char, keyboard_1_data;
  wire [7:0] inputdata;
  wire [11:0] address;
  wire [15:0] address16, addressdata, aluout, bit_extender_1_out, bit_extender_3_out, bit_extender_4_out,
       multiplexer_1_out, multiplexer_2_out, multiplexer_5_out, multiplexer_6_out, multiplexer_7_out,
       multiplexer_9_out, multiplexer_11_out, multiplexer_12_out, PC_1, PC_1_imm, PCdata, rom_1_data,
       undriven, value, writedata;
  wire [15:7] rsdata;

  Clock Clock (.out(clk));
  PC u_pc_1 (.datain_2(PCdata), .RegWriteEnable(1'b1), .Reset(reset), .Clock(clk), .datain(undriven));
  assign bit_extender_1_out = {{10{imm[5]}}, imm};  // Bit_Extender bit_extender_1
  Adder #(.width(16)) adder_1 (.a(PC_1), .b(bit_extender_1_out), .out(PC_1_imm));  // open: cin, cout
  Adder #(.width(16)) adder_2 (.a(16'h1), .b(undriven), .out(PC_1));  // open: cin, cout
  ROM #(.addrWidth(16), .dataWidth(16)) rom_1 (.addr(undriven), .data(rom_1_data));  // open: sel
  Multiplexer #(.width(16), .enable("false")) multiplexer_1 (
    .in0(PC_1), .in1(PC_1_imm), .out(multiplexer_1_out), .sel(and_1_out));
  and and_1 (and_1_out, bne, equal);
  // Probe on rt
  // Probe on imm
  and and_2 (and_2_out, blt, equal);
  InstructionDecoder instructiondecoder_1 (
    .rs(rs), .rt(rt), .codeline(rom_1_data), .opcode(opcode), .address(address),
    .rd(instructiondecoder_1_rd), .immediate(imm), .shamt(shamt));
  // Probe on rs
  Multiplexer #(.width(16), .enable("false")) multiplexer_2 (
    .in0(multiplexer_1_out), .in1(PC_1_imm), .out(multiplexer_2_out), .sel(and_2_out));
  // Probe on {rsdata, char}
  RegisterFile registerfile_1 (
    .WriteReg(writereg), .WriteData(writedata), .ReadReg1(rs), .ReadReg2(rt), .RegWriteEnable(rwe),
    .Reset(reset), .Clock(clk), .ReadData1({rsdata, char}), .ReadData2(value));
  Multiplexer #(.width(3), .enable("false")) multiplexer_3 (
    .in0(instructiondecoder_1_rd), .in1(rt), .out(multiplexer_3_out), .sel(rdst));
  assign address16 = {{4{1'b0}}, address};  // Bit_Extender bit_extender_2
  // Probe on value
  Multiplexer #(.width(3), .enable("false")) multiplexer_4 (
    .in0(multiplexer_3_out), .in1(3'b111), .out(writereg), .sel(jal));
  Multiplexer #(.width(16), .enable("false")) multiplexer_5 (
    .in0(multiplexer_2_out), .in1(address16), .out(multiplexer_5_out), .sel(jump));
  assign bit_extender_3_out = {{10{imm[5]}}, imm};  // Bit_Extender bit_extender_3
  Multiplexer #(.width(16), .enable("false")) multiplexer_6 (
    .in0(value), .in1(bit_extender_3_out), .out(multiplexer_6_out), .sel(alusrc));
  Multiplexer #(.width(16), .enable("false")) multiplexer_7 (
    .in0(multiplexer_5_out), .in1(address16), .out(multiplexer_7_out), .sel(jr));
  Multiplexer #(.width(16), .enable("false")) multiplexer_8 (
    .in0(multiplexer_11_out), .in1(PC_1), .out(writedata), .sel(jal));
  assign bit_extender_4_out = {{13{1'b0}}, shamt};  // Bit_Extender bit_extender_4
  Multiplexer #(.width(16), .enable("false")) multiplexer_9 (
    .in0(multiplexer_6_out), .in1(bit_extender_4_out), .out(multiplexer_9_out), .sel(shift));
  Multiplexer #(.width(16), .enable("false")) multiplexer_10 (
    .in0(multiplexer_7_out), .in1({rsdata, char}), .out(PCdata), .sel(jal));
  Multiplexer #(.width(16), .enable("false")) multiplexer_11 (
    .in0(multiplexer_12_out), .in1({{8{1'b0}}, inputdata}), .out(multiplexer_11_out), .sel(\input ));
  // Probe on opcode
  ALU alu_1 (
    .i1({rsdata, char}), .i2(multiplexer_9_out), .opcode(opcode), .\output (aluout), .equal(equal),
    .sign(sign));
  Multiplexer #(.width(16), .enable("false")) multiplexer_12 (
    .in0(aluout), .in1(addressdata), .out(multiplexer_12_out), .sel(rwd));
  Control control_1 (
    .opcode(opcode), .rwe(rwe), .rdst(rdst), .alusrc(alusrc), .shift(shift), .rwd(rwd), .mem(mem), .j(j),
    .jal(jal), .jr(jr), .bne(bne), .blt(blt), .\input (\input ), .\output (\output ));
  RAM #(.addrWidth(16), .dataWidth(16), .bus("separate")) ram_1 (
    .addr(aluout), .din(value), .data(addressdata), .str(mem), .clk(not_1_out));  // open: sel, ld, clr
  not not_1 (not_1_out, clk);
  TTY #(.rows(13), .cols(80), .trigger("falling")) tty_1 (.data(char), .clk(clk), .we(\output ), .clr(reset));
  not not_2 (not_2_out, clk);
  Keyboard keyboard_1 (.clk(not_2_out), .re(\input ), .clr(reset), .avail(keyboard_1_avail), .data(keyboard_1_data));
  not not_3 (inputdata[7], keyboard_1_avail);
  Multiplexer #(.width(7), .enable("false")) multiplexer_13 (
    .in0({7{1'b0}}), .in1(keyboard_1_data), .out(inputdata[6:0]), .sel(keyboard_1_avail));

  // Other names for the same wires on the sheet: rsdata[6:0] = char
endmodule

module RegisterFile (
  input  [2:0] WriteReg,
  input  [15:0] WriteData,
  input  [2:0] ReadReg1,
  input  [2:0] ReadReg2,
  input  RegWriteEnable,
  input  Reset,
  input  Clock,
  output [15:0] ReadData1,
  output [15:0] ReadData2
);

  wire and_1_out, and_2_out, and_3_out, and_4_out, and_5_out, and_6_out, and_7_out, and_8_out,
       decoder_1_out0, decoder_1_out1, decoder_1_out2, decoder_1_out3, decoder_1_out4, decoder_1_out5,
       decoder_1_out6, decoder_1_out7;
  wire [15:0] register_1_q, register_2_q, register_3_q, register_4_q, register_5_q, register_6_q,
       register_7_q, register_8_q;

  Decoder #(.select(3), .enable("false")) decoder_1 (
    .out0(decoder_1_out0), .out1(decoder_1_out1), .out2(decoder_1_out2), .out3(decoder_1_out3),
    .out4(decoder_1_out4), .out5(decoder_1_out5), .out6(decoder_1_out6), .out7(decoder_1_out7), .sel(WriteReg));
  and and_1 (and_1_out, decoder_1_out0, RegWriteEnable);
  and and_2 (and_2_out, decoder_1_out1, RegWriteEnable);
  and and_3 (and_3_out, decoder_1_out2, RegWriteEnable);
  and and_4 (and_4_out, decoder_1_out3, RegWriteEnable);
  and and_5 (and_5_out, decoder_1_out4, RegWriteEnable);
  and and_6 (and_6_out, decoder_1_out5, RegWriteEnable);
  and and_7 (and_7_out, decoder_1_out6, RegWriteEnable);
  and and_8 (and_8_out, decoder_1_out7, RegWriteEnable);
  // Probe on register_1_q
  Register #(.width(16), .trigger("falling")) register_1 (
    .D(WriteData), .en(and_1_out), .Q(register_1_q), .clk(Clock), .clr(Reset));
  // Probe on register_2_q
  Register #(.width(16), .trigger("falling")) register_2 (
    .D(WriteData), .en(and_2_out), .Q(register_2_q), .clk(Clock), .clr(Reset));
  // Probe on register_3_q
  Register #(.width(16), .trigger("falling")) register_3 (
    .D(WriteData), .en(and_3_out), .Q(register_3_q), .clk(Clock), .clr(Reset));
  // Probe on register_4_q
  Register #(.width(16), .trigger("falling")) register_4 (
    .D(WriteData), .en(and_4_out), .Q(register_4_q), .clk(Clock), .clr(Reset));
  // Probe on register_5_q
  Register #(.width(16), .trigger("falling")) register_5 (
    .D(WriteData), .en(and_5_out), .Q(register_5_q), .clk(Clock), .clr(Reset));
  // Probe on register_6_q
  Register #(.width(16), .trigger("falling")) register_6 (
    .D(WriteData), .en(and_6_out), .Q(register_6_q), .clk(Clock), .clr(Reset));
  // Probe on register_7_q
  Register #(.width(16), .trigger("falling")) register_7 (
    .D(WriteData), .en(and_7_out), .Q(register_7_q), .clk(Clock), .clr(Reset));
  // Probe on register_8_q
  Register #(.width(16), .trigger("falling")) register_8 (
    .D(WriteData), .en(and_8_out), .Q(register_8_q), .clk(Clock), .clr(Reset));
  Multiplexer #(.select(3), .width(16), .enable("false")) multiplexer_1 (
    .in0(register_1_q), .in1(register_2_q), .in2(register_3_q), .in3(register_4_q), .in4(register_5_q),
    .in5(register_6_q), .in6(register_7_q), .in7(register_8_q), .out(ReadData1), .sel(ReadReg1));
  Multiplexer #(.select(3), .width(16), .enable("false")) multiplexer_2 (
    .in0(register_1_q), .in1(register_2_q), .in2(register_3_q), .in3(register_4_q), .in4(register_5_q),
    .in5(register_6_q), .in6(register_7_q), .in7(register_8_q), .out(ReadData2), .sel(ReadReg2));

  // Other names for the same wires on the sheet: clk = Clock; data[15:0] = WriteData; R1[2:0] = ReadReg1;
  //   R2[2:0] = ReadReg2; WE = RegWriteEnable
endmodule

module ALU (
  input  [15:0] i1,
  input  [15:0] i2,
  input  [3:0] opcode,
  output [15:0] \output ,
  output equal,
  output sign
);

  wire [3:0] bit_extender_1_out, bit_extender_2_out;
  wire [14:0] xor_2_out;
  wire [15:0] adder_1_out, adder_2_out, adder_3_out, adder_4_out, not_1_out, shifter_1_out, shifter_2_out,
       subtractor_1_out, subtractor_2_out, xor_1_out;

  Bit_Extender #(.in_width(16), .out_width(4)) bit_extender_1 (.in(i2), .out(bit_extender_1_out));
  Bit_Extender #(.in_width(16), .out_width(4)) bit_extender_2 (.in(i2), .out(bit_extender_2_out));
  assign not_1_out = ~i1;  // NOT_Gate not_1, 16 bits wide
  assign xor_1_out = i1 ^ i2;  // XOR_Gate xor_1, 16 bits wide
  Adder #(.width(16)) adder_1 (.a(i1), .b(i2), .out(adder_1_out));  // open: cin, cout
  Adder #(.width(16)) adder_2 (.a(i1), .b(i2), .out(adder_2_out));  // open: cin, cout
  Subtractor #(.width(16)) subtractor_1 (.a(i1), .b(i2), .out(subtractor_1_out));  // open: bin, bout
  Shifter #(.width(16), .shift("ar")) shifter_1 (.in(i1), .\dist (bit_extender_1_out), .out(shifter_1_out));
  Shifter #(.width(16)) shifter_2 (.in(i1), .\dist (bit_extender_2_out), .out(shifter_2_out));
  Adder #(.width(16)) adder_3 (.a(i1), .b(i2), .out(adder_3_out));  // open: cin, cout
  Adder #(.width(16)) adder_4 (.a(i1), .b(i2), .out(adder_4_out));  // open: cin, cout
  Subtractor #(.width(16)) subtractor_2 (.a(i1), .b(i2), .out(subtractor_2_out));  // open: bin, bout
  assign {sign, xor_2_out} = subtractor_2_out ^ {16{1'b0}};  // XOR_Gate xor_2, 16 bits wide
  or or_1 (equal, xor_2_out[0], xor_2_out[1], xor_2_out[2], xor_2_out[3], xor_2_out[4], xor_2_out[5], xor_2_out[6], xor_2_out[7], xor_2_out[8], xor_2_out[9], xor_2_out[10], xor_2_out[11], xor_2_out[12], xor_2_out[13], xor_2_out[14], sign);
  Multiplexer #(.select(4), .width(16), .enable("false")) multiplexer_1 (
    .in0(not_1_out), .in1(xor_1_out), .in2(adder_1_out), .in3(adder_2_out), .in4(subtractor_1_out),
    .in5(shifter_1_out), .in6(shifter_2_out), .in7(adder_3_out), .in8(adder_4_out), .in9({16{1'b0}}),
    .in10({16{1'b0}}), .in11({16{1'b0}}), .in12({16{1'b0}}), .in13({16{1'b0}}), .in14({16{1'b0}}),
    .in15({16{1'b0}}), .out(\output ), .sel(opcode));
endmodule

module InstructionDecoder (
  input  [15:0] codeline,
  output [3:0] opcode,
  output [2:0] rs,
  output [2:0] rt,
  output [2:0] rd,
  output [11:0] address,
  output [2:0] shamt,
  output [5:0] immediate
);


  assign address = codeline[11:0];
  assign immediate = codeline[5:0];
  assign opcode = codeline[15:12];
  assign rd = codeline[5:3];
  assign rs = codeline[11:9];
  assign rt = codeline[8:6];
  assign shamt = codeline[2:0];
endmodule

module Control (
  input  [3:0] opcode,
  output rwe,
  output rdst,
  output alusrc,
  output shift,
  output rwd,
  output mem,
  output j,
  output jal,
  output jr,
  output bne,
  output blt,
  output \input ,
  output \output 
);

  wire add, addi, \not , sll, sra, sub, \xor ;

  Decoder #(.select(4), .enable("false")) decoder_1 (
    .out0(\not ), .out1(\xor ), .out2(addi), .out3(add), .out4(sub), .out5(sra), .out6(sll), .out7(rwd),
    .out8(mem), .out9(j), .out10(jal), .out11(jr), .out12(bne), .out13(blt), .out14(\input ),
    .out15(\output ), .sel(opcode));
  or or_1 (rwe, \not , \xor , addi, add, sub, sra, sll, rwd, jal, \input );
  or or_2 (rdst, addi, rwd);
  or or_3 (alusrc, addi, rwd, mem);
  or or_4 (shift, sra, sll);

  // Other names for the same wires on the sheet: lw = rwd; sw = mem
endmodule

module PC (
  input  [15:0] datain,
  input  [15:0] datain_2,
  input  RegWriteEnable,
  input  Reset,
  input  Clock
);

  D_Flip_Flop d_ff_1 (
    .clk(Clock), .D(datain_2[0]), .Q(datain[0]), .en(RegWriteEnable), .reset(Reset));  // open: Qn, preset
  D_Flip_Flop d_ff_2 (
    .clk(Clock), .D(datain_2[1]), .Q(datain[1]), .en(RegWriteEnable), .reset(Reset));  // open: Qn, preset
  D_Flip_Flop d_ff_3 (
    .clk(Clock), .D(datain_2[2]), .Q(datain[2]), .en(RegWriteEnable), .reset(Reset));  // open: Qn, preset
  D_Flip_Flop d_ff_4 (
    .clk(Clock), .D(datain_2[3]), .Q(datain[3]), .en(RegWriteEnable), .reset(Reset));  // open: Qn, preset
  D_Flip_Flop d_ff_5 (
    .clk(Clock), .D(datain_2[4]), .Q(datain[4]), .en(RegWriteEnable), .reset(Reset));  // open: Qn, preset
  D_Flip_Flop d_ff_6 (
    .clk(Clock), .D(datain_2[5]), .Q(datain[5]), .en(RegWriteEnable), .reset(Reset));  // open: Qn, preset
  D_Flip_Flop d_ff_7 (
    .clk(Clock), .D(datain_2[6]), .Q(datain[6]), .en(RegWriteEnable), .reset(Reset));  // open: Qn, preset
  D_Flip_Flop d_ff_8 (
    .clk(Clock), .D(datain_2[7]), .Q(datain[7]), .en(RegWriteEnable), .reset(Reset));  // open: Qn, preset
  D_Flip_Flop d_ff_9 (
    .clk(Clock), .D(datain_2[8]), .Q(datain[8]), .en(RegWriteEnable), .reset(Reset));  // open: Qn, preset
  D_Flip_Flop d_ff_10 (
    .clk(Clock), .D(datain_2[9]), .Q(datain[9]), .en(RegWriteEnable), .reset(Reset));  // open: Qn, preset
  D_Flip_Flop d_ff_11 (
    .clk(Clock), .D(datain_2[10]), .Q(datain[10]), .en(RegWriteEnable), .reset(Reset));  // open: Qn, preset
  D_Flip_Flop d_ff_12 (
    .clk(Clock), .D(datain_2[11]), .Q(datain[11]), .en(RegWriteEnable), .reset(Reset));  // open: Qn, preset
  D_Flip_Flop d_ff_13 (
    .clk(Clock), .D(datain_2[12]), .Q(datain[12]), .en(RegWriteEnable), .reset(Reset));  // open: Qn, preset
  D_Flip_Flop d_ff_14 (
    .clk(Clock), .D(datain_2[13]), .Q(datain[13]), .en(RegWriteEnable), .reset(Reset));  // open: Qn, preset
  D_Flip_Flop d_ff_15 (
    .clk(Clock), .D(datain_2[14]), .Q(datain[14]), .en(RegWriteEnable), .reset(Reset));  // open: Qn, preset
  D_Flip_Flop d_ff_16 (
    .clk(Clock), .D(datain_2[15]), .Q(datain[15]), .en(RegWriteEnable), .reset(Reset));  // open: Qn, preset

  // Other names for the same wires on the sheet: clk = Clock; WE = RegWriteEnable
endmodule
